// Logisim project Lab2.circ as structural Verilog
module Lab2_1 (
  input  in_1,
  input  in_2,
  input  in_3,
  input  in_4,
  input  in_5,
  output out_6,
  output out_7,
  output out_8
);

  wire nand_1_out, nand_2_out, nand_3_out;

  nand nand_1 (nand_1_out, in_1, in_2);
  nand nand_2 (nand_2_out, in_3, in_3);
  nand nand_3 (nand_3_out, in_4, in_4);
  nand nand_4 (out_8, in_5, in_5);
  nand nand_5 (out_6, nand_1_out, nand_1_out);
  nand nand_6 (out_7, nand_2_out, nand_3_out);

  // Notes on the sheet:
  //   1
  //   2
  //   3
endmodule

module Lab2_2 (
  input  A,
  input  B,
  input  A2,
  input  B2,
  input  in_5,
  input  in_6,
  output out_7,
  output out_8
);

  wire and_1_out, and_2_out, nand_1_out, nand_2_out, nand_3_out, not_1_out, not_2_out;

  not not_1 (not_1_out, A);
  not not_2 (not_2_out, B2);
  nand nand_1 (nand_1_out, in_5, in_6);
  and and_1 (and_1_out, not_1_out, B);
  and and_2 (and_2_out, A2, not_2_out);
  nand nand_2 (nand_2_out, in_5, nand_1_out);
  nand nand_3 (nand_3_out, nand_1_out, in_6);
  or or_1 (out_7, and_1_out, and_2_out);
  nand nand_4 (out_8, nand_2_out, nand_3_out);

  // Notes on the sheet:
  //   1
endmodule

module Lab2_3 (
  input  A,
  input  B,
  input  CarryIn,
  input  in_4,
  input  in_5,
  input  in_6,
  input  in_7,
  input  in_8,
  input  in_9,
  input  in_10,
  input  in_11,
  input  in_12,
  output out_13,
  output CarryOut,
  output out_15,
  output out_16,
  output out_17,
  output out_18,
  output out_19
);

  wire and_1_out, and_2_out, and_3_out, and_4_out, and_5_out, and_6_out, and_7_out, and_8_out, and_9_out,
       and_10_out, or_2_out, or_3_out, or_4_out, xor_1_out, xor_3_out, xor_5_out, xor_7_out, xor_9_out;

  xor xor_1 (xor_1_out, A, B);
  and and_1 (and_1_out, A, B);
  and and_2 (and_2_out, xor_1_out, CarryIn);
  xor xor_2 (out_13, xor_1_out, CarryIn);
  or or_1 (CarryOut, and_2_out, and_1_out);
  xor xor_3 (xor_3_out, in_4, in_5);
  and and_3 (and_3_out, in_4, in_5);
  xor xor_4 (out_15, xor_3_out, in_6);
  and and_4 (and_4_out, xor_3_out, in_6);
  or or_2 (or_2_out, and_4_out, and_3_out);
  xor xor_5 (xor_5_out, in_7, in_8);
  and and_5 (and_5_out, in_7, in_8);
  xor xor_6 (out_16, xor_5_out, or_2_out);
  and and_6 (and_6_out, xor_5_out, or_2_out);
  or or_3 (or_3_out, and_6_out, and_5_out);
  xor xor_7 (xor_7_out, in_9, in_10);
  and and_7 (and_7_out, in_9, in_10);
  and and_8 (and_8_out, xor_7_out, or_3_out);
  xor xor_8 (out_17, xor_7_out, or_3_out);
  or or_4 (or_4_out, and_8_out, and_7_out);
  and and_9 (and_9_out, in_11, in_12);
  xor xor_9 (xor_9_out, in_11, in_12);
  xor xor_10 (out_18, xor_9_out, or_4_out);
  and and_10 (and_10_out, xor_9_out, or_4_out);
  or or_5 (out_19, and_10_out, and_9_out);
endmodule

module Lab2_4 (
  input  in_1,
  input  in_2,
  input  in_3,
  input  [1:0] in_4,
  input  in_5,
  input  in_6,
  output out_7,
  output out_8
);

  wire adder_1_out, and_1_out, multiplexer_1_out, multiplexer_2_out, not_1_out, not_2_out, or_1_out;

  not not_1 (not_1_out, in_2);
  not not_2 (not_2_out, in_5);
  Multiplexer multiplexer_1 (.in0(in_2), .in1(not_1_out), .out(multiplexer_1_out), .sel(in_3));
  Multiplexer multiplexer_2 (.in0(in_5), .in1(not_2_out), .out(multiplexer_2_out), .sel(in_6));
  and and_1 (and_1_out, multiplexer_1_out, multiplexer_2_out);
  or or_1 (or_1_out, multiplexer_1_out, multiplexer_2_out);
  Adder #(.width(1)) adder_1 (
    .a(multiplexer_1_out), .b(multiplexer_2_out), .out(adder_1_out), .cin(in_1), .cout(out_8));
  Multiplexer #(.select(2)) multiplexer_3 (
    .in0(and_1_out), .in1(or_1_out), .in2(adder_1_out), .out(out_7), .sel(in_4));  // open: in3
endmodule

module Lab2_5 (
  input  in_1,
  input  [7:0] in_2,
  input  in_3,
  input  [7:0] in_4,
  input  in_5,
  input  [2:0] in_6,
  output [7:0] out_7
);

  wire comparator_1_eq;
  wire [7:0] adder_1_out, adder_2_out, bit_extender_1_out, divider_1_out, multiplexer_1_out,
       multiplier_1_out, not_1_out, not_2_out, not_3_out, xor_1_out;

  assign not_1_out = ~in_2;  // NOT_Gate not_1, 8 bits wide
  assign not_2_out = ~in_4;  // NOT_Gate not_2, 8 bits wide
  Multiplexer #(.width(8)) multiplexer_1 (.in0(in_2), .in1(not_1_out), .out(multiplexer_1_out), .sel(in_3));
  Multiplexer #(.width(8)) multiplexer_2 (.in0(in_4), .in1(not_2_out), .out(multiplexer_1_out), .sel(in_5));
  assign not_3_out = ~multiplexer_1_out;  // NOT_Gate not_3, 8 bits wide
  Adder adder_1 (.a(multiplexer_1_out), .b(multiplexer_1_out), .out(adder_1_out), .cin(in_1));  // open: cout
  Adder adder_2 (.a(multiplexer_1_out), .b(not_3_out), .out(adder_2_out), .cin(in_1));  // open: cout
  Multiplier multiplier_1 (.a(multiplexer_1_out), .b(multiplexer_1_out), .out(multiplier_1_out));  // open: cin, cout
  Divider divider_1 (.a(multiplexer_1_out), .b(multiplexer_1_out), .out(divider_1_out));  // open: upper, rem
  assign xor_1_out = multiplexer_1_out ^ multiplexer_1_out;  // XOR_Gate xor_1, 8 bits wide
  Comparator comparator_1 (.a(multiplexer_1_out), .b(multiplexer_1_out), .eq(comparator_1_eq));  // open: gt, lt
  assign bit_extender_1_out = {{7{comparator_1_eq}}, comparator_1_eq};  // Bit_Extender bit_extender_1
  Multiplexer #(.select(3), .width(8)) multiplexer_3 (
    .in0(adder_1_out), .in1(adder_2_out), .in2(multiplier_1_out), .in3(divider_1_out), .in4(xor_1_out),
    .in5(bit_extender_1_out), .out(out_7), .sel(in_6));  // open: in6, in7
endmodule
